// Digital circuit Arcane_8.dig as structural Verilog
module Arcane_8 (
  input  Clock,
  input  [2:0] ALU_Control,
  input  [7:0] Reset,
  input  [7:0] Data_In,
  input  inc,
  input  dec,
  input  load,
  input  [1:0] Chip_Select,
  input  Data_IO,
  input  load_2,
  input  count,
  input  write,
  input  read,
  input  read_2,
  input  read_3,
  input  read_4,
  input  write_2,
  input  read_5,
  input  write_3,
  input  read_6,
  input  write_4,
  input  read_7,
  input  write_5,
  input  in_30,
  input  in_31,
  input  in_32,
  input  in_33,
  input  in_34,
  input  in_35,
  input  in_36,
  input  write_6,
  input  write_7,
  input  in_39,
  input  in_40,
  input  read_8,
  input  RegA_Read,
  input  RegA_Write,
  input  RegB_Read,
  input  RegB_Write,
  input  RegC_Read,
  input  RegC_Write,
  input  RegD_Read,
  input  RegD_Write,
  input  Stack_Write,
  input  Stack_Read,
  input  Stack_Dec,
  input  Stack_Inc,
  input  PCH_Load,
  input  PCH_Read,
  input  PCL_Load,
  input  PCL_Read,
  input  PC_Inc,
  input  ALU_Add,
  input  RegM_Read,
  input  ALU_Sub,
  input  ALU_And,
  input  ALU_Or,
  input  ALU_Xor,
  input  ALU_Not,
  input  ALU_LSL,
  input  ALU_LSR,
  input  RegX_Read,
  input  RegX_Write,
  input  RegY_Read,
  input  RegY_Write,
  input  in_72,
  input  write_8,
  input  read_9,
  output Zero,
  output Carry,
  output [15:0] Addr_Out,
  output [7:0] Data_Out,
  output carry_2,
  output carry_3,
  output [7:0] Out
);

  wire [7:0] driver_1_out;

  Decoder #(.Selector_Bits(2)) decoder_1 (.sel(Chip_Select));  // open: out_0, out_1, out_2, out_3
  StackPointer_Arc8 stackpointer_arc8_1 ();
  ProgramCounter_Arc8 H ();
  ProgramCounter_Arc8 L ();
  Register_Arc8 register_arc8_1 (.clock(Clock), .reset(in_33), .write(Reset[0]));  // open: CS, read, out
  Register_Arc8 register_arc8_2 (.clock(Clock), .reset(in_34), .write(Reset[0]));  // open: CS, read, out
  Register_Arc8 register_arc8_3 (.clock(Clock), .reset(in_35), .write(Reset[0]));  // open: CS, read, out
  Register_Arc8 register_arc8_4 (.clock(Clock), .reset(in_36), .write(Reset[0]));  // open: CS, read, out
  EEPROM #(.AddrBits(16), .Bits(8)) Main (.A(Addr_Out), .CS(in_72), .WE(write_8), .OE(read_9), .D(Out));
  ALU_Arc8 alu_arc8_1 ();
  IO_Register_Arc8 X (.clock(Clock), .reset(in_39), .in(Reset));  // open: CS, write, out
  IO_Register_Arc8 Y (.clock(Clock), .reset(in_40), .in(Reset));  // open: CS, write, out
  Accumulator_Arc8 Acu ();
  assign driver_1_out = Data_IO ? Data_In : 8'bz;  // Driver driver_1
  assign Data_Out = ~Data_IO ? driver_1_out : 8'bz;  // DriverInvSel driverinvsel_1
  // Pins of 1 and 8 bits meet at Reset

  // Other names for the same wires on the sheet: Mem_CS = in_72; PC_H_CS = in_31; PC_L_CS = in_32; RA_CS = in_33;
  //   RB_CS = in_34; RC_CS = in_35; RD_CS = in_36; RX_CS = in_39; RY_CS = in_40; SP_CS = in_30

  // Notes on the sheet:
  //   TBD: Control Unit
  //   TBD: Timing Controller
  //   TBD: Memory Access
  //   TBD: Redesign ALU
endmodule
