// Digital circuit ALU_Arc8.dig as structural Verilog
module ALU_Arc8 (
  input  [7:0] X,
  input  [7:0] Y,
  input  [2:0] control,
  output [7:0] data,
  output carry,
  output zero
);

  wire add_1_c_o, add_2_c_o, add_3_c_o, add_4_c_o, add_6_c_o, add_7_c_o, add_8_c_o, and_9_out, and_10_out,
       and_12_out, and_13_out, and_14_out, and_15_out, and_16_out, and_17_out, and_18_out, and_19_out,
       and_20_out, and_21_out, and_23_out, CS_ADD, CS_AND, CS_LEFT, CS_OR, CS_RIGHT, CS_SUB, CS_XOR,
       not_1_out, not_2_out, or_11_out, or_12_out, or_13_out, or_14_out, or_16_out, or_17_out, or_18_out,
       xor_1_out, xor_2_out, xor_4_out, xor_8_out, xor_12_out, xor_14_out, xor_15_out, xor_16_out,
       xor_17_out, xor_18_out;
  wire [7:0] add_1_s, and_1_out, and_11_out, or_1_out, xor_3_out;

  Decoder #(.Selector_Bits(3)) decoder_1 (
    .sel(control), .out_0(CS_ADD), .out_1(CS_SUB), .out_2(CS_AND), .out_3(CS_OR), .out_4(CS_XOR),
    .out_5(CS_LEFT), .out_6(CS_RIGHT));  // open: out_7
  xor xor_1 (xor_1_out, Y[0], CS_SUB);
  xor xor_2 (xor_2_out, Y[1], CS_SUB);
  and and_1 (and_1_out[0], X[0], Y[0]);
  or or_1 (or_1_out[0], X[0], Y[0]);
  xor xor_3 (xor_3_out[0], X[0], Y[0]);
  Add add_1 (.a(X[0]), .b(xor_1_out), .c_i(CS_SUB), .s(add_1_s[0]), .c_o(add_1_c_o));
  Add add_2 (.a(X[1]), .b(xor_2_out), .c_i(add_1_c_o), .s(add_1_s[1]), .c_o(add_2_c_o));
  Add add_3 (.a(X[2]), .b(xor_4_out), .c_i(add_2_c_o), .s(add_1_s[2]), .c_o(add_3_c_o));
  Add add_4 (.a(X[3]), .b(xor_8_out), .c_i(add_3_c_o), .s(add_1_s[3]), .c_o(add_4_c_o));
  xor xor_4 (xor_4_out, Y[2], CS_SUB);
  and and_2 (and_1_out[2], X[2], Y[2]);
  and and_3 (and_1_out[4], X[4], Y[4]);
  and and_4 (and_1_out[6], X[6], Y[6]);
  or or_2 (or_1_out[2], X[2], Y[2]);
  or or_3 (or_1_out[4], X[4], Y[4]);
  or or_4 (or_1_out[6], X[6], Y[6]);
  xor xor_5 (xor_3_out[2], X[2], Y[2]);
  xor xor_6 (xor_3_out[4], X[4], Y[4]);
  xor xor_7 (xor_3_out[6], X[6], Y[6]);
  xor xor_8 (xor_8_out, Y[3], CS_SUB);
  and and_5 (and_1_out[1], X[1], Y[1]);
  and and_6 (and_1_out[3], X[3], Y[3]);
  and and_7 (and_1_out[5], X[5], Y[5]);
  or or_5 (or_1_out[1], X[1], Y[1]);
  or or_6 (or_1_out[3], X[3], Y[3]);
  or or_7 (or_1_out[5], X[5], Y[5]);
  xor xor_9 (xor_3_out[1], X[1], Y[1]);
  xor xor_10 (xor_3_out[3], X[3], Y[3]);
  xor xor_11 (xor_3_out[5], X[5], Y[5]);
  xor xor_12 (xor_12_out, Y[4], CS_SUB);
  and and_8 (and_1_out[7], X[7], Y[7]);
  or or_8 (or_1_out[7], X[7], Y[7]);
  xor xor_13 (xor_3_out[7], X[7], Y[7]);
  xor xor_14 (xor_14_out, Y[5], CS_SUB);
  xor xor_15 (xor_15_out, Y[6], CS_SUB);
  Add add_5 (.a(X[7]), .b(xor_16_out), .c_i(add_6_c_o), .s(add_1_s[7]), .c_o(carry));
  Add add_6 (.a(X[6]), .b(xor_15_out), .c_i(add_7_c_o), .s(add_1_s[6]), .c_o(add_6_c_o));
  Add add_7 (.a(X[5]), .b(xor_14_out), .c_i(add_8_c_o), .s(add_1_s[5]), .c_o(add_7_c_o));
  Add add_8 (.a(X[4]), .b(xor_12_out), .c_i(add_4_c_o), .s(add_1_s[4]), .c_o(add_8_c_o));
  xor xor_16 (xor_16_out, Y[7], CS_SUB);
  assign data = CS_AND ? and_1_out : 8'bz;  // Driver driver_1
  assign data = CS_OR ? or_1_out : 8'bz;  // Driver driver_2
  assign data = CS_XOR ? xor_3_out : 8'bz;  // Driver driver_3
  not not_1 (not_1_out, and_9_out);
  assign data = xor_17_out ? and_11_out : 8'bz;  // Driver driver_4
  assign data = xor_18_out ? add_1_s : 8'bz;  // Driver driver_5
  and and_9 (and_9_out, CS_LEFT, not_2_out);
  and and_10 (and_10_out, and_9_out, X[0]);
  xor xor_17 (xor_17_out, CS_RIGHT, CS_LEFT);
  xor xor_18 (xor_18_out, CS_ADD, CS_SUB);
  not not_2 (not_2_out, CS_RIGHT);
  and and_11 (and_11_out[0], X[1], not_1_out);
  or or_9 (and_11_out[1], and_13_out, and_10_out);
  and and_12 (and_12_out, and_9_out, X[1]);
  and and_13 (and_13_out, X[2], not_1_out);
  and and_14 (and_14_out, and_9_out, X[2]);
  or or_10 (and_11_out[2], and_15_out, and_12_out);
  or or_11 (or_11_out, data[3], or_12_out);
  or or_12 (or_12_out, data[2], or_13_out);
  or or_13 (or_13_out, data[1], data[0]);
  and and_15 (and_15_out, X[3], not_1_out);
  or or_14 (or_14_out, data[7], or_16_out);
  and and_16 (and_16_out, and_9_out, X[3]);
  or or_15 (and_11_out[3], and_17_out, and_14_out);
  not not_3 (zero, or_14_out);
  or or_16 (or_16_out, or_17_out, data[6]);
  or or_17 (or_17_out, or_18_out, data[5]);
  or or_18 (or_18_out, or_11_out, data[4]);
  and and_17 (and_17_out, X[4], not_1_out);
  or or_19 (and_11_out[4], and_19_out, and_16_out);
  and and_18 (and_18_out, and_9_out, X[4]);
  and and_19 (and_19_out, X[5], not_1_out);
  or or_20 (and_11_out[5], and_21_out, and_18_out);
  and and_20 (and_20_out, and_9_out, X[5]);
  and and_21 (and_21_out, X[6], not_1_out);
  and and_22 (and_11_out[7], and_9_out, X[6]);
  or or_21 (and_11_out[6], and_23_out, and_20_out);
  and and_23 (and_23_out, X[7], not_1_out);

  // Notes on the sheet:
  //   control: [ 0 - Add ]   
  //   [ 1 - Sub ]   
  //   [ 2 - And]   
  //   [ 3 - Or ]   
  //   [ 4 - Xor ]   
  //   [ 5 - Left Shift ]   
  //   [ 6 - Right Shift ]   
  //   [ 7 - Undefined ]
  //   ADD/SUB
  //   AND
  //   OR
  //   XOR
  //   BIT SHIFT
  //   ZERO
endmodule
