// Digital circuit ProgramCounter_Arc8.dig as structural Verilog
module ProgramCounter_Arc8 (
  input  write,
  input  count,
  input  clock,
  input  reset,
  input  read,
  input  CS,
  output [7:0] data,
  output [7:0] addr,
  output carry
);

  wire and_1_out, and_2_out, and_3_out, and_4_out, and_5_out, and_6_out, and_7_out, and_8_out, and_9_out,
       and_10_out, and_11_out, and_12_out, and_13_out, and_14_out, and_15_out, and_16_out, and_17_out,
       and_18_out, and_19_out, and_20_out, and_21_out, and_22_out, and_23_out, and_24_out, and_25_out,
       and_26_out, and_27_out, and_28_out, and_29_out, and_31_out, and_32_out, and_33_out, and_34_out,
       nor_1_out, nor_2_out, nor_4_out, nor_5_out, nor_6_out, nor_7_out, nor_8_out, nor_9_out, nor_11_out,
       nor_12_out, nor_13_out, nor_14_out, nor_15_out, nor_16_out, nor_18_out, nor_19_out, nor_20_out,
       nor_21_out, nor_22_out, nor_23_out, nor_25_out, nor_26_out, nor_27_out, nor_28_out, nor_29_out,
       nor_30_out, nor_32_out, nor_33_out, nor_34_out, nor_35_out, nor_36_out, nor_37_out, nor_39_out,
       nor_40_out, nor_41_out, nor_42_out, nor_43_out, nor_44_out, nor_46_out, nor_47_out, nor_48_out,
       nor_49_out, nor_50_out, nor_51_out, nor_53_out, nor_54_out, nor_55_out, nor_56_out, or_1_out,
       or_2_out, xor_1_out, xor_2_out, xor_3_out, xor_4_out, xor_5_out, xor_6_out, xor_7_out, xor_8_out;
  wire [7:0] driver_1_out, nor_3_out;

  or or_1 (or_1_out, count, reset, read);
  and and_1 (and_1_out, ~read, write, CS);  // And
  assign driver_1_out = and_1_out ? data : 8'bz;  // Driver driver_1
  assign data = and_2_out ? driver_1_out : 8'bz;  // Driver driver_2
  assign addr = and_2_out ? driver_1_out : 8'bz;  // Driver driver_3
  and and_2 (and_2_out, read, ~write, CS);  // And
  and and_3 (and_3_out, count, driver_1_out[0]);
  xor xor_1 (xor_1_out, count, driver_1_out[0]);
  or or_2 (or_2_out, ~write, read);  // Or
  assign driver_1_out = or_2_out ? nor_3_out : 8'bz;  // Driver driver_4
  and and_4 (and_4_out, or_1_out, xor_1_out);
  nor nor_1 (nor_1_out, nor_5_out, clock);
  nor nor_2 (nor_2_out, nor_6_out, nor_1_out);
  and and_5 (and_5_out, clock, nor_2_out);
  nor nor_3 (nor_3_out[0], nor_7_out, and_5_out);
  and and_6 (and_6_out, and_3_out, driver_1_out[1]);
  xor xor_2 (xor_2_out, and_3_out, driver_1_out[1]);
  nor nor_4 (nor_4_out, nor_7_out, or_1_out);
  nor nor_5 (nor_5_out, nor_4_out, and_4_out, clock);
  nor nor_6 (nor_6_out, nor_5_out, reset, nor_2_out);
  and and_7 (and_7_out, nor_6_out, clock);
  nor nor_7 (nor_7_out, and_7_out, nor_3_out[0]);
  and and_8 (and_8_out, or_1_out, xor_2_out);
  nor nor_8 (nor_8_out, nor_12_out, clock);
  nor nor_9 (nor_9_out, nor_13_out, nor_8_out);
  and and_9 (and_9_out, clock, nor_9_out);
  nor nor_10 (nor_3_out[1], nor_14_out, and_9_out);
  and and_10 (and_10_out, and_6_out, driver_1_out[2]);
  xor xor_3 (xor_3_out, and_6_out, driver_1_out[2]);
  nor nor_11 (nor_11_out, nor_14_out, or_1_out);
  nor nor_12 (nor_12_out, nor_11_out, and_8_out, clock);
  nor nor_13 (nor_13_out, nor_12_out, reset, nor_9_out);
  and and_11 (and_11_out, nor_13_out, clock);
  nor nor_14 (nor_14_out, and_11_out, nor_3_out[1]);
  and and_12 (and_12_out, or_1_out, xor_3_out);
  nor nor_15 (nor_15_out, nor_19_out, clock);
  nor nor_16 (nor_16_out, nor_20_out, nor_15_out);
  and and_13 (and_13_out, clock, nor_16_out);
  nor nor_17 (nor_3_out[2], nor_21_out, and_13_out);
  and and_14 (and_14_out, and_10_out, driver_1_out[3]);
  xor xor_4 (xor_4_out, and_10_out, driver_1_out[3]);
  nor nor_18 (nor_18_out, nor_21_out, or_1_out);
  nor nor_19 (nor_19_out, nor_18_out, and_12_out, clock);
  nor nor_20 (nor_20_out, nor_19_out, reset, nor_16_out);
  and and_15 (and_15_out, nor_20_out, clock);
  nor nor_21 (nor_21_out, and_15_out, nor_3_out[2]);
  and and_16 (and_16_out, or_1_out, xor_4_out);
  nor nor_22 (nor_22_out, nor_26_out, clock);
  nor nor_23 (nor_23_out, nor_27_out, nor_22_out);
  and and_17 (and_17_out, clock, nor_23_out);
  nor nor_24 (nor_3_out[3], nor_28_out, and_17_out);
  and and_18 (and_18_out, and_14_out, driver_1_out[4]);
  xor xor_5 (xor_5_out, and_14_out, driver_1_out[4]);
  nor nor_25 (nor_25_out, nor_28_out, or_1_out);
  nor nor_26 (nor_26_out, nor_25_out, and_16_out, clock);
  nor nor_27 (nor_27_out, nor_26_out, reset, nor_23_out);
  and and_19 (and_19_out, nor_27_out, clock);
  nor nor_28 (nor_28_out, and_19_out, nor_3_out[3]);
  and and_20 (and_20_out, or_1_out, xor_5_out);
  nor nor_29 (nor_29_out, nor_33_out, clock);
  nor nor_30 (nor_30_out, nor_34_out, nor_29_out);
  and and_21 (and_21_out, clock, nor_30_out);
  nor nor_31 (nor_3_out[4], nor_35_out, and_21_out);
  and and_22 (and_22_out, and_18_out, driver_1_out[5]);
  xor xor_6 (xor_6_out, and_18_out, driver_1_out[5]);
  nor nor_32 (nor_32_out, nor_35_out, or_1_out);
  nor nor_33 (nor_33_out, nor_32_out, and_20_out, clock);
  nor nor_34 (nor_34_out, nor_33_out, reset, nor_30_out);
  and and_23 (and_23_out, nor_34_out, clock);
  nor nor_35 (nor_35_out, and_23_out, nor_3_out[4]);
  and and_24 (and_24_out, or_1_out, xor_6_out);
  nor nor_36 (nor_36_out, nor_40_out, clock);
  nor nor_37 (nor_37_out, nor_41_out, nor_36_out);
  and and_25 (and_25_out, clock, nor_37_out);
  nor nor_38 (nor_3_out[5], nor_42_out, and_25_out);
  and and_26 (and_26_out, and_22_out, driver_1_out[6]);
  xor xor_7 (xor_7_out, and_22_out, driver_1_out[6]);
  nor nor_39 (nor_39_out, nor_42_out, or_1_out);
  nor nor_40 (nor_40_out, nor_39_out, and_24_out, clock);
  nor nor_41 (nor_41_out, nor_40_out, reset, nor_37_out);
  and and_27 (and_27_out, nor_41_out, clock);
  nor nor_42 (nor_42_out, and_27_out, nor_3_out[5]);
  and and_28 (and_28_out, or_1_out, xor_7_out);
  nor nor_43 (nor_43_out, nor_47_out, clock);
  nor nor_44 (nor_44_out, nor_48_out, nor_43_out);
  and and_29 (and_29_out, clock, nor_44_out);
  nor nor_45 (nor_3_out[6], nor_49_out, and_29_out);
  and and_30 (carry, and_26_out, driver_1_out[7]);
  xor xor_8 (xor_8_out, and_26_out, driver_1_out[7]);
  nor nor_46 (nor_46_out, nor_49_out, or_1_out);
  nor nor_47 (nor_47_out, nor_46_out, and_28_out, clock);
  nor nor_48 (nor_48_out, nor_47_out, reset, nor_44_out);
  and and_31 (and_31_out, nor_48_out, clock);
  nor nor_49 (nor_49_out, and_31_out, nor_3_out[6]);
  and and_32 (and_32_out, or_1_out, xor_8_out);
  nor nor_50 (nor_50_out, nor_54_out, clock);
  nor nor_51 (nor_51_out, nor_55_out, nor_50_out);
  and and_33 (and_33_out, clock, nor_51_out);
  nor nor_52 (nor_3_out[7], nor_56_out, and_33_out);
  nor nor_53 (nor_53_out, nor_56_out, or_1_out);
  nor nor_54 (nor_54_out, nor_53_out, and_32_out, clock);
  nor nor_55 (nor_55_out, nor_54_out, reset, nor_51_out);
  and and_34 (and_34_out, nor_55_out, clock);
  nor nor_56 (nor_56_out, and_34_out, nor_3_out[7]);
endmodule
