// Digital circuit Register_Arc8.dig as structural Verilog
module Register_Arc8 (
  input  clock,
  input  CS,
  input  reset,
  input  read,
  input  write,
  output [7:0] out
);

  wire and_1_out, and_2_out, and_3_out, and_4_out, and_5_out, and_6_out, and_7_out, and_8_out, and_9_out,
       and_10_out, and_11_out, and_12_out, and_13_out, and_14_out, and_15_out, and_16_out, and_17_out,
       and_18_out, and_19_out, nor_1_out, nor_2_out, nor_4_out, nor_5_out, nor_6_out, nor_7_out, nor_8_out,
       nor_10_out, nor_11_out, nor_12_out, nor_13_out, nor_14_out, nor_16_out, nor_17_out, nor_18_out,
       nor_19_out, nor_20_out, nor_22_out, nor_23_out, nor_24_out, nor_25_out, nor_26_out, nor_28_out,
       nor_29_out, nor_30_out, nor_31_out, nor_32_out, nor_34_out, nor_35_out, nor_36_out, nor_37_out,
       nor_38_out, nor_40_out, nor_41_out, nor_42_out, nor_43_out, nor_44_out, nor_46_out, nor_47_out,
       nor_48_out;
  wire [7:0] driver_2_out, nor_3_out;

  and and_1 (and_1_out, CS, write, ~read);  // And
  assign out = and_2_out ? driver_2_out : 8'bz;  // Driver driver_1
  assign driver_2_out = and_1_out ? out : 8'bz;  // Driver driver_2
  and and_2 (and_2_out, CS, ~write, read);  // And
  and and_3 (and_3_out, ~read, write);  // And
  assign driver_2_out = ~and_3_out ? nor_3_out : 8'bz;  // DriverInvSel driverinvsel_1
  nor nor_1 (nor_1_out, nor_4_out, clock);
  nor nor_2 (nor_2_out, nor_5_out, nor_1_out);
  and and_4 (and_4_out, clock, nor_2_out);
  nor nor_3 (nor_3_out[0], nor_6_out, and_4_out);
  nor nor_4 (nor_4_out, driver_2_out[0], clock);
  nor nor_5 (nor_5_out, nor_4_out, reset, nor_2_out);
  and and_5 (and_5_out, nor_5_out, clock);
  nor nor_6 (nor_6_out, and_5_out, nor_3_out[0]);
  nor nor_7 (nor_7_out, nor_10_out, clock);
  nor nor_8 (nor_8_out, nor_11_out, nor_7_out);
  and and_6 (and_6_out, clock, nor_8_out);
  nor nor_9 (nor_3_out[1], nor_12_out, and_6_out);
  nor nor_10 (nor_10_out, driver_2_out[1], clock);
  nor nor_11 (nor_11_out, nor_10_out, reset, nor_8_out);
  and and_7 (and_7_out, nor_11_out, clock);
  nor nor_12 (nor_12_out, and_7_out, nor_3_out[1]);
  nor nor_13 (nor_13_out, nor_16_out, clock);
  nor nor_14 (nor_14_out, nor_17_out, nor_13_out);
  and and_8 (and_8_out, clock, nor_14_out);
  nor nor_15 (nor_3_out[2], nor_18_out, and_8_out);
  nor nor_16 (nor_16_out, driver_2_out[2], clock);
  nor nor_17 (nor_17_out, nor_16_out, reset, nor_14_out);
  and and_9 (and_9_out, nor_17_out, clock);
  nor nor_18 (nor_18_out, and_9_out, nor_3_out[2]);
  nor nor_19 (nor_19_out, nor_22_out, clock);
  nor nor_20 (nor_20_out, nor_23_out, nor_19_out);
  and and_10 (and_10_out, clock, nor_20_out);
  nor nor_21 (nor_3_out[3], nor_24_out, and_10_out);
  nor nor_22 (nor_22_out, driver_2_out[3], clock);
  nor nor_23 (nor_23_out, nor_22_out, reset, nor_20_out);
  and and_11 (and_11_out, nor_23_out, clock);
  nor nor_24 (nor_24_out, and_11_out, nor_3_out[3]);
  nor nor_25 (nor_25_out, nor_28_out, clock);
  nor nor_26 (nor_26_out, nor_29_out, nor_25_out);
  and and_12 (and_12_out, clock, nor_26_out);
  nor nor_27 (nor_3_out[4], nor_30_out, and_12_out);
  nor nor_28 (nor_28_out, driver_2_out[4], clock);
  nor nor_29 (nor_29_out, nor_28_out, reset, nor_26_out);
  and and_13 (and_13_out, nor_29_out, clock);
  nor nor_30 (nor_30_out, and_13_out, nor_3_out[4]);
  nor nor_31 (nor_31_out, nor_34_out, clock);
  nor nor_32 (nor_32_out, nor_35_out, nor_31_out);
  and and_14 (and_14_out, clock, nor_32_out);
  nor nor_33 (nor_3_out[5], nor_36_out, and_14_out);
  nor nor_34 (nor_34_out, driver_2_out[5], clock);
  nor nor_35 (nor_35_out, nor_34_out, reset, nor_32_out);
  and and_15 (and_15_out, nor_35_out, clock);
  nor nor_36 (nor_36_out, and_15_out, nor_3_out[5]);
  nor nor_37 (nor_37_out, nor_40_out, clock);
  nor nor_38 (nor_38_out, nor_41_out, nor_37_out);
  and and_16 (and_16_out, clock, nor_38_out);
  nor nor_39 (nor_3_out[6], nor_42_out, and_16_out);
  nor nor_40 (nor_40_out, driver_2_out[6], clock);
  nor nor_41 (nor_41_out, nor_40_out, reset, nor_38_out);
  and and_17 (and_17_out, nor_41_out, clock);
  nor nor_42 (nor_42_out, and_17_out, nor_3_out[6]);
  nor nor_43 (nor_43_out, nor_46_out, clock);
  nor nor_44 (nor_44_out, nor_47_out, nor_43_out);
  and and_18 (and_18_out, clock, nor_44_out);
  nor nor_45 (nor_3_out[7], nor_48_out, and_18_out);
  nor nor_46 (nor_46_out, driver_2_out[7], clock);
  nor nor_47 (nor_47_out, nor_46_out, reset, nor_44_out);
  and and_19 (and_19_out, nor_47_out, clock);
  nor nor_48 (nor_48_out, and_19_out, nor_3_out[7]);
endmodule
